# Fritzing sketch BreadBoardSchema (saved by Fritzing 0.9.2b)
breadboards: 1

parts:
  Componente1 = Arduino Micro (Rev3)
  R1 = Resistor [tolerance=±5% resistance=10k package=THT]
  Rx1 = mystery part, 4 pins [chip_label=?]
  Componente2 = Adafruit BMP180
  DHT1 = DHT11 Humitidy and Temperature Sensor
  C1 = Ceramic Capacitor [capacitance=100nF package="100 mil [THT, multilayer]"]

nets:
  N1: Componente1.D1/TX, Rx1.pin1
  N2: Componente1.D0/RX, Rx1.pin2
  N3: Componente1.D5_PWM, R1.Pin_0, DHT1.DATA
  GND: Componente1.GND, Rx1.pin3, Componente2.GND, DHT1.GND, C1.1
  5V: Componente1.5V, R1.Pin_1, Rx1.pin4, Componente2.+5V, DHT1.VDD, C1.0
  N4: Componente1.A5, Componente2.SCL
  N5: Componente1.A4, Componente2.SDA

notes:
  TX

custom parts:
  Adafruit BMP180: This precision sensor from Bosch is the best low-cost sensing solution for measuring barometric pressure and temperature. Because pressure changes with altitude you can also use it as an altimeter! The sensor is soldered onto a PCB with a 3.3V regulator, I2C level shifter and pull-up resistors on the I2C pins. The BMP180 is the next-generation of sensors from Bosch, and replaces the BMP085.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
  DHT11 Humitidy and Temperature Sensor: DHT11 Humidity and Temperature Sensor
