# Fritzing sketch VeroBoardSchema (saved by Fritzing 0.9.2b)
stripboards: 1

parts:
  Componente1 = Arduino Micro (Rev3)  # not connected
  Rx2 = mystery part, 4 pins [chip_label=?]
  R2 = Resistor [tolerance=±5% resistance=10k package=THT]
  Componente2 = Adafruit BMP180
  DHT1 = DHT11 Humitidy and Temperature Sensor
  C1 = Ceramic Capacitor [capacitance=100nF package="100 mil [THT, multilayer]"]

nets:
  GND: Rx2.pin2, Rx2.pin3, Componente2.GND, DHT1.GND, C1.1
  +5V: Rx2.pin4, R2.Pin_1, Componente2.+5V, DHT1.VDD, C1.0
  N1: R2.Pin_0, Componente2.SCL, Componente2.SDA, DHT1.DATA

notes:
  TX
  <-- interruzioni

custom parts:
  Adafruit BMP180: This precision sensor from Bosch is the best low-cost sensing solution for measuring barometric pressure and temperature. Because pressure changes with altitude you can also use it as an altimeter! The sensor is soldered onto a PCB with a 3.3V regulator, I2C level shifter and pull-up resistors on the I2C pins. The BMP180 is the next-generation of sensors from Bosch, and replaces the BMP085.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
  DHT11 Humitidy and Temperature Sensor: DHT11 Humidity and Temperature Sensor
